# Fritzing sketch EnergyMeter (saved by Fritzing 0.9.2b)
breadboards: 1

parts:
  Part1 = TRRS 3.5mm Jack Breakout
  TRINKET1 = Trinket 5V
  R1 = Resistor [tolerance=±5% resistance=33 package="2010 [SMD]"]
  C1 = Electrolytic Capacitor [capacitance=10μF voltage=20V package="0605 [SMD, electrolytic]"]
  R2 = Resistor [tolerance=±5% resistance=10k package="2010 [SMD]"]
  R3 = Resistor [tolerance=±5% resistance=10k package="2010 [SMD]"]

nets:
  N1: Part1.SLEEVE, R1.Pin_1, C1.+, R2.Pin_0, R3.Pin_1
  N2: Part1.TIP, TRINKET1.no_name_yet#7, R1.Pin_0
  N3: TRINKET1.no_name_yet#2, C1.-, R2.Pin_1
  N4: TRINKET1.no_name_yet#6, R3.Pin_0

custom parts:
  Trinket 5V: Adafruit Trinket 5V
